// Digital circuit Calculator.dig as structural Verilog
module Calculator (
  output out_1,
  output out_2,
  output out_3,
  output out_4,
  output out_5,
  output out_6,
  output out_7,
  output out_8
);

  wire _0, _1, _2, _3, _4, _5, _6, _7, _8, _9, and_1_out, and_2_out, and_3_out, and_4_out, and_5_out,
       and_6_out, and_7_out, and_8_out, and_9_out, and_10_out, and_11_out, and_12_out, and_13_out,
       and_14_out, and_15_out, and_16_out, C, clicked, comparator_1_lt, comparator_2_lt, comparator_3_eq,
       comparator_3_lt, d1_on, d2_on, d3_on, delay_1_out, delay_2_out, diff_minus, dividebyzero, eq, eq__eq,
       error, Light_Display_3_q, minus, mul_overflow, multiplexer_4_out, multiplexer_8_out, not_1_out,
       not_2_out, Op1, Op2, or_1_out, or_2_out, or_3_out, or_4_out, or_5_out, or_6_out, or_8_out, or_9_out,
       or_11_out, or_12_out, plus, plus__plus, selected, sum_overflow, tunnel, tunnel_t, tunnel_t_t,
       tunnel_t_t_t, X, XX;
  wire [1:0] priorityencoder_2_num;
  wire [3:0] d11, d12, d13, d14, d21, d22, d23, d24, d31, d32, d33, d34, key;
  wire [15:0] add_1_s, add_2_s, add_3_s, diff_result, div_1_q, div_1_r, div_2_q, div_2_r, div_3_q, div_3_r,
       div_4_q, div_4_r, div_5_q, div_5_r, div_6_q, div_6_r, div_7_q, div_7_r, div_9_q, div_9_r, div_10_q,
       div_10_r, div_result, mul_result, multiplexer_2_out, multiplexer_3_out, multiplexer_5_out, neg_1_out,
       num1, num2, result, sub_1_s, sum_result;
  wire [31:0] click_count, click_count2, mul_1_mul, mul_2_mul;

  PriorityEncoder #(.Selector_Bits(4)) priorityencoder_1 (
    .in0(_0), .in1(_1), .in2(_2), .in3(_3), .in4(_4), .in5(_5), .in6(_6), .in7(_7), .in8(_8), .in9(_9),
    .in10(1'b0), .in11(1'b0), .in12(1'b0), .in13(1'b0), .in14(1'b0), .in15(1'b0), .num(key));  // open: any
  and and_1 (and_1_out, eq, d2_on, Op2);
  and and_2 (and_2_out, plus, d1_on, Op1);
  and and_3 (and_3_out, tunnel, d1_on, Op1);
  and and_4 (and_4_out, X, d1_on, Op1);
  and and_5 (and_5_out, tunnel_t_t, d1_on, Op1);
  PriorityEncoder #(.Selector_Bits(2)) priorityencoder_2 (
    .in0(plus__plus), .in1(tunnel_t), .in2(XX), .in3(tunnel_t_t_t), .num(priorityencoder_2_num));  // open: any
  RS_FF_AS Equal (.S(and_1_out), .R(C), .Q(eq__eq));  // open: nQ
  RS_FF_AS Addition (.S(and_2_out), .R(C), .Q(plus__plus));  // open: nQ
  RS_FF_AS Subtraction (.S(and_3_out), .R(C), .Q(tunnel_t));  // open: nQ
  RS_FF_AS Multiplication (.S(and_4_out), .R(C), .Q(XX));  // open: nQ
  RS_FF_AS Division (.S(and_5_out), .R(C), .Q(tunnel_t_t_t));  // open: nQ
  Multiplexer #(.Selector_Bits(2), .Bits(16)) multiplexer_1 (
    .sel(priorityencoder_2_num), .in_0(sum_result), .in_1(diff_result), .in_2(mul_result), .in_3(div_result),
    .out(result));
  Seven_Seg_Hex seven_seg_hex_1 (.d(d14), .dp(1'b0));
  Comparator #(.Bits(32)) comparator_1 (.a(click_count), .b(32'h4), .gt(out_3), .eq(out_4), .lt(comparator_1_lt));
  Seven_Seg_Hex seven_seg_hex_2 (.d(d13), .dp(1'b0));
  Comparator #(.Bits(32)) comparator_2 (.a(click_count2), .b(32'h4), .gt(out_6), .eq(out_7), .lt(comparator_2_lt));
  and and_6 (and_6_out, comparator_2_lt, not_1_out, Op2);
  not not_1 (not_1_out, eq__eq);
  and and_7 (and_7_out, comparator_1_lt, Op1);
  Seven_Seg_Hex seven_seg_hex_3 (.d(d12), .dp(1'b0));
  or or_1 (or_1_out, and_7_out, C);
  Seven_Seg_Hex seven_seg_hex_4 (.d(d11), .dp(1'b0));
  or or_2 (or_2_out, C, clicked);
  Delay delay_1 (.in(or_2_out), .out(delay_1_out));
  or or_3 (or_3_out, and_6_out, C);
  or or_4 (or_4_out, C, clicked);
  Register #(.Bits(16)) register_1 (.D(multiplexer_2_out), .C(delay_2_out), .en(or_1_out), .Q(num1));
  Delay delay_2 (.in(or_4_out), .out(delay_2_out));
  Register #(.Bits(16)) register_2 (.D(multiplexer_3_out), .C(delay_1_out), .en(or_3_out), .Q(num2));
  LED u_plus (.in(plus__plus));
  LED led (.in(tunnel_t));
  LED u_X (.in(XX));
  LED led_2 (.in(tunnel_t_t_t));
  Mul #(.Bits(16)) mul_1 (.a(num1), .b(16'ha), .mul(mul_1_mul));
  Mul #(.Bits(16)) mul_2 (.a(num2), .b(16'ha), .mul(mul_2_mul));
  Multiplexer #(.Bits(16)) multiplexer_2 (.sel(C), .in_0(add_1_s), .in_1({16{1'b0}}), .out(multiplexer_2_out));
  Seven_Seg_Hex seven_seg_hex_5 (.d(d24), .dp(1'b0));
  Multiplexer #(.Bits(16)) multiplexer_3 (.sel(C), .in_0(add_2_s), .in_1({16{1'b0}}), .out(multiplexer_3_out));
  Add #(.Bits(16)) add_1 (.a(mul_1_mul[15:0]), .b({{12{1'b0}}, key}), .c_i(1'b0), .s(add_1_s), .c_o(out_1));
  Button u__1 (.out(_1));
  Button u__4 (.out(_4));
  Button u__7 (.out(_7));
  Button u_C (.out(C));
  Add #(.Bits(16)) add_2 (.a(mul_2_mul[15:0]), .b({{12{1'b0}}, key}), .c_i(1'b0), .s(add_2_s), .c_o(out_5));
  Seven_Seg_Hex seven_seg_hex_6 (.d(d23), .dp(1'b0));
  Button u__2 (.out(_2));
  Button u__5 (.out(_5));
  Button u__8 (.out(_8));
  Button u__0 (.out(_0));
  Seven_Seg_Hex seven_seg_hex_7 (.d(d22), .dp(1'b0));
  Div #(.Bits(16)) div_1 (.a(num2), .b(16'h3e8), .q(div_1_q), .r(div_1_r));
  Div #(.Bits(16)) div_2 (.a(num1), .b(16'h3e8), .q(div_2_q), .r(div_2_r));
  Button u__3 (.out(_3));
  Button u__6 (.out(_6));
  Button u__9 (.out(_9));
  Button u_eq (.out(eq));
  Seven_Seg_Hex seven_seg_hex_8 (.d(d21), .dp(1'b0));
  or or_5 (or_5_out, clicked, C);
  assign d14 = d1_on ? div_2_q[3:0] : 4'bz;  // Driver driver_1
  Div #(.Bits(16)) div_3 (.a(div_2_r), .b(16'h64), .q(div_3_q), .r(div_3_r));
  Button plus_2 (.out(plus));
  Button button (.out(tunnel));
  Button X_2 (.out(X));
  Button button_2 (.out(tunnel_t_t));
  or or_6 (or_6_out, clicked, C);
  assign d24 = d2_on ? div_1_q[3:0] : 4'bz;  // Driver driver_2
  Div #(.Bits(16)) div_4 (.a(div_1_r), .b(16'h64), .q(div_4_q), .r(div_4_r));
  Counter #(.Bits(32)) counter_1 (.en(Op2), .C(or_6_out), .clr(C), .out(click_count2), .ovf(out_8));
  Counter #(.Bits(32)) counter_2 (.en(Op1), .C(or_5_out), .clr(C), .out(click_count), .ovf(out_2));
  assign d13 = d1_on ? div_3_q[3:0] : 4'bz;  // Driver driver_3
  Div #(.Bits(16)) div_5 (.a(div_3_r), .b(16'ha), .q(div_5_q), .r(div_5_r));
  LED u_MINUS (.in(minus));
  assign d23 = d2_on ? div_4_q[3:0] : 4'bz;  // Driver driver_4
  Div #(.Bits(16)) div_6 (.a(div_4_r), .b(16'ha), .q(div_6_q), .r(div_6_r));
  assign d12 = d1_on ? div_5_q[3:0] : 4'bz;  // Driver driver_5
  assign d11 = d1_on ? div_5_r[3:0] : 4'bz;  // Driver driver_6
  Seven_Seg_Hex seven_seg_hex_9 (.d(d34), .dp(1'b0));
  assign d22 = d2_on ? div_6_q[3:0] : 4'bz;  // Driver driver_7
  assign d21 = d2_on ? div_6_r[3:0] : 4'bz;  // Driver driver_8
  or or_7 (selected, plus, tunnel, X, tunnel_t_t);
  Seven_Seg_Hex seven_seg_hex_10 (.d(d33), .dp(1'b0));
  or or_8 (or_8_out, _0, _1, _2, _3, _4);
  or or_9 (or_9_out, _5, _6, _7, _8, _9);
  RS_FF_AS rs_ff_as_1 (.S(and_9_out), .R(C), .Q(Op2), .nQ(Op1));
  Seven_Seg_Hex seven_seg_hex_11 (.d(d32), .dp(1'b0));
  and and_8 (and_8_out, diff_minus, tunnel_t);
  and and_9 (and_9_out, selected, d1_on);
  LED u_Error (.in(error));
  Multiplexer multiplexer_4 (.sel(eq__eq), .in_0(1'b0), .in_1(and_8_out), .out(multiplexer_4_out));
  or or_10 (clicked, or_8_out, or_9_out);
  Seven_Seg_Hex seven_seg_hex_12 (.d(d31), .dp(1'b0));
  RS_FF_AS Minus_2 (.S(multiplexer_4_out), .R(C), .Q(minus));  // open: nQ
  Multiplexer #(.Bits(16)) multiplexer_5 (.sel(and_11_out), .in_0({16{1'b0}}), .in_1(result), .out(multiplexer_5_out));
  and and_10 (and_10_out, clicked, Op1);
  Div #(.Bits(16)) div_7 (.a(multiplexer_5_out), .b(16'h3e8), .q(div_7_q), .r(div_7_r));
  RS_FF_AS Light_Display_1 (.S(and_10_out), .R(C), .Q(d1_on));  // open: nQ
  Add #(.Bits(16)) add_3 (.a(num1), .b(num2), .c_i(1'b0), .s(add_3_s));  // open: c_o
  Sub #(.Bits(16)) sub_1 (.a(num1), .b(num2), .c_i(1'b0), .s(sub_1_s));  // open: c_o
  Mul #(.applicationType("IVERILOG")) u_Mul_3 (.a(num1), .b(num2), .out(mul_result), .overflow(mul_overflow));
  Div #(.applicationType("IVERILOG")) u_Div_8 (.a(num1), .b(num2), .out(div_result), .error(dividebyzero));
  not not_2 (not_2_out, error);
  and and_11 (and_11_out, eq__eq, not_2_out);
  and and_12 (and_12_out, eq__eq, d2_on, Op2);
  and and_13 (and_13_out, sum_overflow, plus__plus);
  and and_14 (and_14_out, dividebyzero, tunnel_t_t_t);
  and and_15 (and_15_out, mul_overflow, XX);
  assign d34 = d3_on ? div_7_q[3:0] : 4'bz;  // Driver driver_9
  Div #(.Bits(16)) div_9 (.a(div_7_r), .b(16'h64), .q(div_9_q), .r(div_9_r));
  RS_FF_AS Light_Display_3 (.S(and_12_out), .R(C), .Q(Light_Display_3_q));  // open: nQ
  Comparator #(.Bits(16)) comparator_3 (
    .a(add_3_s), .b(16'h270f), .gt(sum_overflow), .eq(comparator_3_eq), .lt(comparator_3_lt));
  Comparator #(.Signed("true"), .Bits(16)) comparator_4 (.a(sub_1_s), .b({16{1'b0}}), .lt(diff_minus));  // open: gt, eq
  or or_11 (or_11_out, and_13_out, and_14_out, and_15_out);
  and and_16 (and_16_out, clicked, Op2);
  or or_12 (or_12_out, comparator_3_eq, comparator_3_lt);
  Neg #(.Bits(16)) neg_1 (.in(sub_1_s), .out(neg_1_out));
  assign d33 = d3_on ? div_9_q[3:0] : 4'bz;  // Driver driver_10
  Div #(.Bits(16)) div_10 (.a(div_9_r), .b(16'ha), .q(div_10_q), .r(div_10_r));
  Multiplexer multiplexer_6 (.sel(error), .in_0(Light_Display_3_q), .in_1(1'b0), .out(d3_on));
  Multiplexer #(.Bits(16)) multiplexer_7 (.sel(diff_minus), .in_0(sub_1_s), .in_1(neg_1_out), .out(diff_result));
  Multiplexer multiplexer_8 (.sel(eq__eq), .in_0(1'b0), .in_1(or_11_out), .out(multiplexer_8_out));
  assign d32 = d3_on ? div_10_q[3:0] : 4'bz;  // Driver driver_11
  assign d31 = d3_on ? div_10_r[3:0] : 4'bz;  // Driver driver_12
  RS_FF_AS Light_Display_2 (.S(and_16_out), .R(C), .Q(d2_on));  // open: nQ
  assign sum_result = or_12_out ? add_3_s : 16'bz;  // Driver driver_13
  RS_FF_AS Error_2 (.S(multiplexer_8_out), .R(C), .Q(error));  // open: nQ

  // Notes on the sheet:
  //   Number Encoder
  //   Operation Memory
  //   Operation Selection
  //   Operant 1
  //   User Interface
  //   Operant 2
  //   Keyboard
  //   =
  //   Order Control
  //   Negative Button Memory
  //   Key Click Event
  //   Display Light on off
  //   Result Display
  //   Addition
  //   Subtraction
  //   Multiplication
  //   Division
  //   Error Button Memory
endmodule

/* Code of Mul:
module Mul (
    input signed [15:0] a,
    input signed [15:0] b,
    output signed [15:0] out,
    output overflow
);

    wire signed [31:0] full_result;

    assign full_result = a * b;
    assign out = full_result[15:0];
    assign overflow = (full_result > 32'sd9999) || (full_result < -32'sd9999);

endmodule
*/

/* Code of Div:
module Div (
    input signed [15:0] a,
    input signed [15:0] b,
    output signed [15:0] out,
    output error
);

    assign error = (b == 0);

    assign out = (b == 0) ? 16'sd0 : (a / b);

endmodule
*/
